# Fritzing sketch SmartBlinds (saved by Fritzing 0.9.3b)
breadboards: 1

parts:
  Part1 = Arduino Pro Mini v13
  BAT1 = Battery Holders [package=battery-aa-panel]
  D1 = SOLAR-IXYS [package=solarbit-12x1]
  Part3 = Micro Lipo Charger
  J1 = Basic Servo
  Q1 = PNP-Transistor [package="SOT-23 [SMD]"]
  R1 = Resistor [tolerance=±5% resistance=1k package="0603 [SMD]"]
  Part2 = PowerBoost 500 Charger
  T1 = LM35 Temperature Sensor [package="TO92 [THT]"]
  R2 = Photocell (LDR) [package=THT]
  R3 = Resistor [tolerance=±5% resistance=10k package="0603 [SMD]"]
  C1 = Electrolytic Capacitor [capacitance=1μF package="0405 [SMD, electrolytic]"]

nets:
  GND: Part1.GND, J1.gnd, Part2.GND, T1.GND, R3.Pin_1, C1.-
  N1: Part1.VCC, T1.+Vs, R2.pin_0
  N2: Part1.A3, R2.pin_1, R3.Pin_0
  N3: Part1.A2, T1.Vout
  N4: Part1.A1, BAT1.+, Part3.VBAT, Part2.VBAT_IN
  N5: Part1.A0, D1.A, Part3.5V
  N6: Part1.D11_PWM/MOSI, R1.Pin_1
  N7: Part1.D10_PWM/SS, J1.pulse
  N8: BAT1.-, D1.C, Part3.GND
  N9: J1.vcc, Q1.1, C1.+
  N10: Q1.2, Part2.5.0V
  N11: Q1.0, R1.Pin_0

custom parts:
  Micro Lipo Charger: Oh so handy, this little lipo charger is so small and easy to use you can keep it on your desk or mount it easily into any project! Simply plug it via any MicroUSB cable into a USB port and a 3.7V/4.2V lithium polymer or lithium ion rechargeable battery into the JST plug on the other end. There are two LEDs - one red and one green. While charging, the red LED is lit. When the battery is fully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
